# Fritzing sketch diagram (saved by Fritzing 0.9.3b)

parts:
  Part1 = Arduino Uno (Rev3) - ICSP
  Part2 = Bluetooth HC-05 Macho
  U1 = LCD-16X2 [package=lcd-16x2_noholes]
  LCM1602_IIC1 = LCM1602 IIC [part_number="LCM1602 IIC" chip_label="LCM1602 IIC" package="DIP (Dual Inline) [THT]"]
  LED1 = LED - 3mm [color="Red (633nm)" package="3 mm [THT]"]
  LED2 = LED - 3mm [color="Green (560nm)" package="3 mm [THT]"]

nets:
  N1: Part1.A4/SDA, LCM1602_IIC1.SDA
  N2: Part1.A5/SCL, LCM1602_IIC1.SCL
  N3: Part1.D10_PWM/SS, Part2.TXD
  N4: Part1.D11_PWM/MOSI, Part2.RXD
  GND: Part1.GND, Part2.GND, LCM1602_IIC1.GND, LED1.cathode, LED2.cathode
  N5: Part1.D4, LED2.anode
  N6: Part1.D6_PWM, LED1.anode
  N7: Part1.3V3, Part2.Key
  VCC: Part1.5V, Part2.VCC, LCM1602_IIC1.VCC
  VSS: U1.VSS, LCM1602_IIC1.VSS
  VDD: U1.VDD, LCM1602_IIC1.VDD
  N8: U1.VO, LCM1602_IIC1.V0
  N9: U1.RS, LCM1602_IIC1.RS
  N10: U1.R_W, LCM1602_IIC1.RW
  N11: U1.E, LCM1602_IIC1.E
  N12: U1.DB0, LCM1602_IIC1.D0
  N13: U1.DB1, LCM1602_IIC1.D1
  N14: U1.DB2, LCM1602_IIC1.D2
  N15: U1.DB3, LCM1602_IIC1.D3
  N16: U1.DB4, LCM1602_IIC1.D4
  N17: U1.DB5, LCM1602_IIC1.D5
  N18: U1.DB6, LCM1602_IIC1.D6
  N19: U1.DB7, LCM1602_IIC1.D7
  N20: U1.A, LCM1602_IIC1.A
  N21: U1.K, LCM1602_IIC1.K
  N22: LCM1602_IIC1.LED_A, LCM1602_IIC1.LED_B

custom parts:
  LCM1602 IIC: I2C-Module to use a 1602 or 2004 LCD on with the wire.h libory Serial LCD Modul
